// Logisim project custom_reg.circ as structural Verilog: 12 circuits, main circuit 1bit_reg
module _1bit_reg (
  input  Clock,
  input  Data,
  input  Clear,
  input  Load,
  output Data_out
);

  wire and_1_out, and_2_out, not_1_out, not_2_out;

  and and_1 (and_1_out, Data, Load);
  not not_1 (not_1_out, Data);
  and and_2 (and_2_out, not_1_out, Load);
  J_K_Flip_Flop j_k_ff_1 (
    .J(and_1_out), .clk(Clock), .K(and_2_out), .Q(Data_out), .preset(1'b0), .en(not_2_out), .reset(Clear));  // open: Qn
  not not_2 (not_2_out, Clear);

  // Notes on the sheet:
  //   Lorenzo McDaniel
  //   OLA5
  //   1bit_reg
endmodule

module Register (
  input  Clock,
  input  [31:0] Data_In,
  input  Load,
  output [31:0] Data_out
);

  Register_part #(.width(32)) register_1 (.D(Data_In), .en(Load), .Q(Data_out), .clk(Clock));  // open: clr

  // Notes on the sheet:
  //   Ola5
  //   Register
  //   Lorenzo McDaniel
endmodule

module BusRegister (
  input  Clock,
  input  [31:0] Data_In,
  input  Load,
  input  Bus,
  output [31:0] Data_out,
  output [31:0] Bus_out
);

  Register_part #(.width(32)) register_1 (.D(Data_In), .en(Load), .Q(Data_out), .clk(Clock));  // open: clr
  assign Bus_out = Bus ? Data_out : 32'bz;  // Controlled_Buffer controlled_buffer_1

  // Notes on the sheet:
  //   Lorenzo McDaniel
  //   OLA5
  //   BusRegister
endmodule

module ClearRegister (
  input  Clear,
  input  Clock,
  input  [31:0] Data_In,
  input  Load,
  input  Bus,
  output [31:0] Data_out,
  output [31:0] Bus_out
);

  Register_part #(.width(32)) register_1 (.D(Data_In), .en(Load), .Q(Data_out), .clk(Clock), .clr(Clear));
  assign Bus_out = Bus ? Data_out : 32'bz;  // Controlled_Buffer controlled_buffer_1

  // Notes on the sheet:
  //   Lorenzo McDaniel
  //   OLA5
  //   ClearRegister
endmodule

module CountRegister (
  input  Clock,
  input  [31:0] Data_In,
  input  Count,
  input  Load,
  input  Bus,
  output [31:0] Data_out,
  output [31:0] Bus_out
);

  wire or_1_out;
  wire [31:0] adder_1_out, multiplexer_1_out;

  Adder #(.width(32)) adder_1 (.a(Data_out), .b(32'h1), .out(adder_1_out));  // open: cin, cout
  Multiplexer #(.width(32)) multiplexer_1 (
    .in0(Data_In), .in1(adder_1_out), .out(multiplexer_1_out), .sel(Count));  // open: en
  or or_1 (or_1_out, Count, Load);
  Register_part #(.width(32)) register_1 (
    .D(multiplexer_1_out), .en(or_1_out), .Q(Data_out), .clk(Clock));  // open: clr
  assign Bus_out = Bus ? Data_out : 32'bz;  // Controlled_Buffer controlled_buffer_1

  // Notes on the sheet:
  //   Lorenzo McDaniel
  //   OLA5
  //   CountRegister
endmodule

module ACC (
  input  Clock,
  input  Clear,
  input  [31:0] Data_In,
  input  Bus,
  input  Load,
  output [31:0] Data_out,
  output [31:0] Bus_out
);

  ClearRegister clearregister_1 (
    .Data_In(Data_In), .Clock(Clock), .Clear(Clear), .Load(Load), .Bus(Bus), .Data_out(Data_out),
    .Bus_out(Bus_out));

  // Notes on the sheet:
  //   Lorenzo McDaniel
  //   OLA5
  //   ACC
endmodule

module AR (
  input  Clock,
  input  [31:0] Data_In,
  input  Load,
  output [31:0] Data_out
);

  Register register_1 (.Data_In(Data_In), .Clock(Clock), .Load(Load), .Data_out(Data_out));

  // Notes on the sheet:
  //   Lorenzo McDaniel
  //   OLA5
  //   AR
endmodule

module DR (
  input  Clock,
  input  [31:0] Data_In,
  input  Bus,
  input  Load,
  output [31:0] Data_out,
  output [31:0] Bus_out
);

  BusRegister busregister_1 (
    .Data_In(Data_In), .Clock(Clock), .Load(Load), .Bus(Bus), .Data_out(Data_out), .Bus_out(Bus_out));

  // Notes on the sheet:
  //   Lorenzo McDaniel
  //   OLA5
  //   DR
endmodule

module IR (
  input  Clock,
  input  [31:0] Data_In,
  input  Load,
  output [31:0] Data_out
);

  Register register_1 (.Data_In(Data_In), .Clock(Clock), .Load(Load), .Data_out(Data_out));

  // Notes on the sheet:
  //   OLA5
  //   IR
  //   Lorenzo McDaniel
endmodule

module OUTR (
  input  Clock,
  input  [31:0] Data_In,
  input  Load,
  output [31:0] Data_out
);

  Register register_1 (.Data_In(Data_In), .Clock(Clock), .Load(Load), .Data_out(Data_out));

  // Notes on the sheet:
  //   OLA5
  //   OUTR
  //   Lorenzo McDaniel
endmodule

module PC (
  input  Clock,
  input  [31:0] Data_out,
  input  [31:0] Data_In,
  input  Count,
  input  Load,
  input  Bus,
  output [31:0] Bus_out
);

  CountRegister countregister_1 (
    .Data_In(Data_In), .Clock(Clock), .Count(Count), .Load(Load), .Bus(Bus), .Data_out(Data_out),
    .Bus_out(Bus_out));

  // Notes on the sheet:
  //   Lorenzo McDaniel
  //   OLA5
  //   PC
endmodule

module R (
  input  Clock,
  input  [31:0] Data_In,
  input  Bus,
  input  Load,
  output [31:0] Data_out,
  output [31:0] Bus_out
);

  BusRegister busregister_1 (
    .Data_In(Data_In), .Clock(Clock), .Load(Load), .Bus(Bus), .Data_out(Data_out), .Bus_out(Bus_out));

  // Notes on the sheet:
  //   OLA5
  //   R
  //   Lorenzo McDaniel
endmodule
